# Fritzing sketch sensorTest (saved by Fritzing 0.9.0b)
breadboards: 2

parts:
  Onderdeel1 = Arduino Uno (Rev3)
  M1 = DC Motor
  Q1 = NPN-Transistor [package="TO92 [THT]"]
  D1 = Rectifier Diode [part_number=1N4001 package="300 mil [THT]"]
  R1 = Resistor [tolerance=±5% resistance=220 package=THT]
  J1 = Piezo Speaker
  J2 = Basic Servo
  LED1 = LED - 5mm [color="Green (560nm)" package="5 mm [THT]"]
  R2 = Resistor [tolerance=±5% resistance=220 package=THT]
  R3 = Photocell (LDR) [package=THT]
  J3 = Basic Force Sensing Resistor (FSR) [package=THT]
  R4 = Rotary Potentiometer (Small) [maximum_resistance=100kΩ package=THT]
  S1 = Pushbutton [package="[THT]"]
  T1 = LM35 Temperature Sensor [package="TO92 [THT]"]
  R6 = Resistor [tolerance=±5% resistance=10k package="0603 [SMD]"]
  R7 = Resistor [tolerance=±5% resistance=10k package="0603 [SMD]"]
  R8 = Resistor [tolerance=±5% resistance=10k package="0603 [SMD]"]

nets:
  N1: Onderdeel1.A0, J3.pin_0, R6.Pin_1
  N2: Onderdeel1.A1, R3.pin_0, R7.Pin_1
  N3: Onderdeel1.A2, R4.wiper
  N4: Onderdeel1.A3, T1.Vout
  N5: Onderdeel1.D8, S1.Pin_1, S1.Pin_2, R8.Pin_1
  N6: Onderdeel1.D10_PWM/SS, J2.pulse
  N7: Onderdeel1.D11_PWM/MOSI, J1.pin2
  N8: Onderdeel1.D13/SCK, R2.Pin_0
  N9: Onderdeel1.D5_PWM, R1.Pin_1
  5V: Onderdeel1.5V, M1.pin_2, D1.cathode, J2.vcc, R3.pin_1, J3.pin_1, R4.leg2, S1.Pin_3, S1.Pin_4
  GND: Onderdeel1.GND, Q1.C, J1.pin1, J2.gnd, LED1.cathode, R4.leg1, T1.+Vs, T1.GND, R6.Pin_0, R7.Pin_0, R8.Pin_0
  N10: M1.pin_1, Q1.E, D1.anode
  N11: Q1.B, R1.Pin_0
  N12: LED1.anode, R2.Pin_1

notes:
  Input
  Output
